// Logisim project HW3-403106681.circ as structural Verilog: 4 circuits, main circuit main
module main (
  input  [31:0] A,
  input  [31:0] B,
  input  Start,
  input  Rst,
  input  Divide,
  output [31:0] Result_Lo,
  output [31:0] Result_Hi,
  output Done
);

  wire ADD, and_1_out, and_2_out, Clk_out, d_ff_1_qn, dec_Count, INIT, ld_Count, ld_P, Start_t;
  wire [0:0] and_3_out;
  wire [5:0] cnt_1_q_count;
  wire [31:0] adder_1_out;
  wire [63:0] DP, shr_1_outp;

  and and_1 (and_1_out, ADD, Result_Lo[0]);
  Adder #(.width(32)) adder_1 (.a(Result_Hi), .b(A), .out(adder_1_out), .cin(1'b0));  // open: cout
  and and_2 (and_2_out, Start, d_ff_1_qn);
  D_Flip_Flop d_ff_1 (.D(and_2_out), .clk(Clk_out), .Q(Start_t), .Qn(d_ff_1_qn));  // open: preset, reset
  or or_1 (ld_P, ld_Count, and_1_out, dec_Count);
  SHR shr_1 (.P({Result_Hi, Result_Lo}), .OUTP(shr_1_outp));
  Multiplexer #(.select(2), .width(64)) multiplexer_1 (
    .in0({{32{1'b0}}, B}), .in1({adder_1_out, Result_Lo}), .in2(shr_1_outp), .in3({Result_Hi, Result_Lo}),
    .out(DP), .sel({dec_Count, and_3_out[0]}));
  and and_3 (and_3_out[0], ADD, Result_Lo[0]);
  Clock #(.phaseOffset(1)) Clk (.out(Clk_out));
  Register #(.width(32)) RA (.D(A), .en(ld_Count), .clk(Clk_out), .clr(Rst));  // open: Q
  Register #(.width(64)) P (.D(DP), .en(ld_P), .clk(Clk_out), .Q({Result_Hi, Result_Lo}), .clr(Rst));
  Cnt cnt_1 (
    .D_Count(6'b100000), .dec_Count(ld_Count), .Rst(Rst), .ld_Count(dec_Count), .Clk(Clk_out),
    .Q_Count(cnt_1_q_count));
  CU cu_1 (
    .Clk(Clk_out), .Start(Start_t), .Z(Done), .Rst(Rst), .INIT(INIT), .LOAD(ld_Count), .ADD(ADD),
    .SHR(dec_Count));
  nor nor_1 (Done, cnt_1_q_count[0], cnt_1_q_count[1], cnt_1_q_count[2], cnt_1_q_count[3], cnt_1_q_count[4], cnt_1_q_count[5]);

  // Other names for the same wires on the sheet: P[63:0] = {Result_Hi, Result_Lo}; P0 = Result_Lo[0]; SH = dec_Count;
  //   ld_RA = ld_Count; LOAD = ld_Count; Z = Done
endmodule

module CU (
  input  Clk,
  input  Start,
  input  Z,
  input  Rst,
  output INIT,
  output LOAD,
  output ADD,
  output SHR
);

  wire and_1_out, and_2_out, D_ADD, D_INIT, D_LOAD, not_1_out, not_2_out;

  D_Flip_Flop d_ff_1 (.D(D_INIT), .clk(Clk), .Q(INIT), .preset(Rst));  // open: Qn, reset
  D_Flip_Flop d_ff_2 (.D(D_LOAD), .clk(Clk), .Q(LOAD), .reset(Rst));  // open: Qn, preset
  D_Flip_Flop d_ff_3 (.D(D_ADD), .clk(Clk), .Q(ADD), .reset(Rst));  // open: Qn, preset
  D_Flip_Flop d_ff_4 (.D(ADD), .clk(Clk), .Q(SHR), .reset(Rst));  // open: Qn, preset
  not not_1 (not_1_out, Start);
  and and_1 (and_1_out, SHR, Z);
  not not_2 (not_2_out, Z);
  and and_2 (and_2_out, not_2_out, SHR);
  and and_3 (D_LOAD, INIT, Start);
  or or_1 (D_INIT, not_1_out, and_1_out);
  or or_2 (D_ADD, and_2_out, LOAD);

  // Other names for the same wires on the sheet: D_SHR = ADD
endmodule

module SHR (
  input  [63:0] P,
  output [63:0] OUTP
);


  assign OUTP = {1'b0, P[63:1]};
endmodule

module Cnt (
  input  [5:0] D_Count,
  input  dec_Count,
  input  Rst,
  input  ld_Count,
  input  Clk,
  output [5:0] Q_Count
);

  wire or_1_out;
  wire [5:0] adder_1_out, multiplexer_1_out;

  Multiplexer #(.width(6)) multiplexer_1 (.in0(D_Count), .in1(adder_1_out), .out(multiplexer_1_out), .sel(dec_Count));
  or or_1 (or_1_out, dec_Count, ld_Count);
  Register #(.width(6)) register_1 (.D(multiplexer_1_out), .en(or_1_out), .clk(Clk), .Q(Q_Count), .clr(Rst));
  Adder #(.width(6)) adder_1 (.a(Q_Count), .b({6{1'b1}}), .out(adder_1_out), .cin(1'b0));  // open: cout
endmodule
